# Fritzing sketch nebenuhr (saved by Fritzing 0.9.2b)
breadboards: 2

parts:
  U1 = atmega328 [package=dip]
  U2 = mystery part, 3 pins [chip_label=?]
  U3 = SWITCH_SPDT [package=kps-1290]
  R1 = Resistor [tolerance=±5% resistance=1M package=THT]
  R2 = Resistor [tolerance=±5% resistance=1k package=THT]
  Q1 = TRANSISTOR_NPN [package=to-92-ammo]
  VCC1 = 4 x AAA Battery Mount
  Q2 = TRANSISTOR_NPN [package=to-92-ammo]
  R4 = Resistor [tolerance=±5% resistance=500k package=THT]
  R5 = Resistor [tolerance=±5% resistance=1M package=THT]
  R6 = Resistor [tolerance=±5% resistance=1M package=THT]
  Q3 = MOSFET-NCHANNEL [package=to-92]
  R7 = Resistor [tolerance=±5% resistance=1k package=THT]
  Q4 = TRANSISTOR_NPN [package=to-92-ammo]
  R8 = Resistor [tolerance=±5% resistance=500k package=THT]
  R9 = Resistor [tolerance=±5% resistance=1k package=THT]
  R10 = Resistor [tolerance=±5% resistance=1M package=THT]

nets:
  N1: U1.RESET, R2.Pin_0
  N2: U1.D1_(TX), R1.Pin_1
  N3: U1.D3_(PWM), Q1.C, Q2.C, R4.Pin_0
  N4: U1.D4, R7.Pin_0
  N5: U2.pin1, Q3.D
  N6: U2.pin2, R5.Pin_1
  N7: U2.pin3, R6.Pin_1
  N8: U3.O, R2.Pin_1, VCC1.+, R4.Pin_1, R10.Pin_1
  N9: U3.P, R1.Pin_0
  N10: U3.S, Q1.E, VCC1.-, Q2.E, Q3.S, R8.Pin_1
  N11: Q1.B, R6.Pin_0
  N12: Q2.B, R5.Pin_0
  N13: Q3.G, R7.Pin_1
  N14: Q4.E, R8.Pin_0
  N15: Q4.B, R9.Pin_1
  N16: Q4.C, R10.Pin_0
